# Fritzing sketch 555LDR (saved by Fritzing 0.9.1b)
stripboards: 2

parts:
  J1 = female pin header, 2 pins [form="♀ (female)"]
  J2 = female pin header, 2 pins [form="♀ (female)"]
  R1 = Resistor [tolerance=±5% resistance=220 package=THT]
  R2 = Resistor [tolerance=±5% resistance=47k package=THT]
  J3 = female pin header, 2 pins [form="♀ (female)"]
  J4 = female pin header, 2 pins [form="♀ (female)"]
  R3 = Resistor [tolerance=±5% resistance=47k package=THT]
  R4 = Resistor [tolerance=±5% resistance=220 package=THT]

nets:
  N1: J1.pin1, R1.Pin_1
  N2: J1.pin2, R1.Pin_0
  N3: J2.pin1, R2.Pin_1
  N4: J2.pin2, R2.Pin_0
  N5: J3.pin1, R4.Pin_1
  N6: J3.pin2, R3.Pin_1
  N7: J4.pin1, R4.Pin_0
  N8: J4.pin2, R3.Pin_0
